// Logisim project lab_04.circ as structural Verilog
module ex_01_a (
  input  Set,
  input  Reset,
  input  in_3,
  input  in_4,
  output out_5,
  output out_6,
  output out_7,
  output out_8
);

  nand nand_1 (out_5, Set, out_6);
  nand nand_2 (out_6, out_5, Reset);
  latch_nand latch_nand_1 (.S(in_3), .R(in_4), .Q(out_7), .QN(out_8));

  // Notes on the sheet:
  //   Latch SR NAND
endmodule

module ex_01_b (
  input  Set_2,
  input  Reset_2,
  input  in_3,
  input  in_4,
  output out_5,
  output out_6,
  output out_7,
  output out_8
);

  nor nor_1 (out_5, Set_2, out_6);
  nor nor_2 (out_6, out_5, Reset_2);
  latch_nor latch_nor_1 (.S(in_3), .R(in_4), .Q(out_7), .QN(out_8));

  // Notes on the sheet:
  //   Latch SR NOR
endmodule

module ex_02_a (
  input  D,
  input  Enable,
  output Q,
  output QN
);

  wire nand_1_out, nand_2_out, not_1_out;

  not not_1 (not_1_out, D);
  nand nand_1 (nand_1_out, D, Enable);
  nand nand_2 (nand_2_out, Enable, not_1_out);
  nand nand_3 (Q, nand_1_out, QN);
  nand nand_4 (QN, Q, nand_2_out);

  // Notes on the sheet:
  //   Latch D NAND
endmodule

module ex_03_a (
);

  D_Flip_Flop d_ff_1 ();  // open: D, clk, Q, Qn, preset, reset
endmodule

module ex_02_b (
  input  D,
  input  Enable,
  output Q,
  output QN
);

  wire nor_1_out, nor_2_out, not_1_out;

  not not_1 (not_1_out, D);
  nor nor_1 (nor_1_out, D, Enable);
  nor nor_2 (nor_2_out, Enable, not_1_out);
  nor nor_3 (Q, nor_1_out, QN);
  nor nor_4 (QN, Q, nor_2_out);
endmodule

module ex_03_b (
  input  CLK,
  input  J,
  input  K,
  output out_4
);

  wire and_1_out, and_2_out, not_1_out, not_2_out, or_1_out;

  not not_1 (not_1_out, out_4);
  not not_2 (not_2_out, K);
  and and_1 (and_1_out, J, not_1_out);
  and and_2 (and_2_out, not_2_out, out_4);
  or or_1 (or_1_out, and_1_out, and_2_out);
  d_jk d_jk_1 ();  // open: J, K, CLRN, PRN, CLK, Q, QN
  D_Flip_Flop d_ff_1 (.D(or_1_out), .clk(CLK), .Q(out_4));  // open: Qn, preset, reset
  d_jk2 d_jk2_1 ();  // open: J, K, CLRN, PRN, CLK, Q, QN

  // Notes on the sheet:
  //   Descritiva
  //   Conversao de D para JK
  //   Logica
endmodule

module ex_03_c (
  input  T,
  input  CLK,
  output Q
);

  wire xor_1_out;

  D_Flip_Flop d_ff_1 (.D(xor_1_out), .clk(CLK), .Q(Q));  // open: Qn, preset, reset
  xor xor_1 (xor_1_out, T, Q);
  d_j d_j_1 ();  // open: T, CLRN, PRN, CLK, Q, QN
  d_j2 d_j2_1 ();  // open: T, CLRN, PRN, CLK, Q, QN

  // Notes on the sheet:
  //   Conversao de D para J
  //   VERSAO DESCRITIVA
  //   VERSAO LOGICA
endmodule

// VHDL entity latch_nand, as the project stores it:
--------------------------------------------------------------------------------
-- Project :
-- File    :
-- Autor   :
-- Date    :
--
--------------------------------------------------------------------------------
-- Description :
--
--------------------------------------------------------------------------------

LIBRARY ieee;
USE ieee.std_logic_1164.all;

ENTITY latch_nand IS
  PORT (
  ------------------------------------------------------------------------------
  --Insert input ports below
    S,R      : IN  std_logic;                    
  ------------------------------------------------------------------------------
  --Insert output ports below
    Q,QN        : OUT std_logic                

    );
END latch_nand;

--------------------------------------------------------------------------------
--Complete your VHDL description below
--------------------------------------------------------------------------------

ARCHITECTURE TypeArchitecture OF latch_nand IS
SIGNAL qstate : std_logic;

BEGIN
  PROCESS(S,R)
  BEGIN
    IF (S = '0' AND R = '1') THEN
      qstate <= '1';
    ELSIF (S = '1' AND R = '0') THEN
      qstate <= '0';
    END IF;
  END PROCESS;


  Q <= qstate;
  QN <= NOT qstate;

END TypeArchitecture;

// VHDL entity latch_nor, as the project stores it:
--------------------------------------------------------------------------------
-- Project :
-- File    :
-- Autor   :
-- Date    :
--
--------------------------------------------------------------------------------
-- Description :
--
--------------------------------------------------------------------------------

LIBRARY ieee;
USE ieee.std_logic_1164.all;

ENTITY latch_nor IS
  PORT (
  ------------------------------------------------------------------------------
  --Insert input ports below
    S,R      : IN  std_logic;                    
  ------------------------------------------------------------------------------
  --Insert output ports below
    Q,QN        : OUT std_logic              

    );
END latch_nor;

--------------------------------------------------------------------------------
--Complete your VHDL description below
--------------------------------------------------------------------------------

ARCHITECTURE TypeArchitecture OF latch_nor IS
SIGNAL qstate : std_logic;

BEGIN
  PROCESS(S,R)
  BEGIN
    IF (S = '1' AND R = '0') THEN
      qstate <= '1';
    ELSIF (S = '0' AND R = '1') THEN
      qstate <= '0';
    END IF;
  END PROCESS;

  Q <= qstate;
  QN <= NOT qstate;

END TypeArchitecture;

// VHDL entity latch_d_nand, as the project stores it:
--------------------------------------------------------------------------------
-- Project :
-- File    :
-- Autor   :
-- Date    :
--
--------------------------------------------------------------------------------
-- Description :
--
--------------------------------------------------------------------------------

LIBRARY ieee;
USE ieee.std_logic_1164.all;

ENTITY latch_d_nand IS
  PORT (
  ------------------------------------------------------------------------------
  --Insert input ports below
    enable,din      : IN  std_logic;                    
  ------------------------------------------------------------------------------
  --Insert output ports below
    q        : OUT std_logic       
    );
END latch_d_nand;

--------------------------------------------------------------------------------
--Complete your VHDL description below
--------------------------------------------------------------------------------

ARCHITECTURE TypeArchitecture OF latch_d_nand IS

BEGIN
	PROCESS(enable,din)
	begin
		if enable = '1' then q <= din;
		end if;
  END PROCESS;

END TypeArchitecture;

// VHDL entity latch_d_nor, as the project stores it:
--------------------------------------------------------------------------------
-- Project :
-- File    :
-- Autor   :
-- Date    :
--
--------------------------------------------------------------------------------
-- Description :
--
--------------------------------------------------------------------------------

LIBRARY ieee;
USE ieee.std_logic_1164.all;

ENTITY latch_d_nor IS
  PORT (
  ------------------------------------------------------------------------------
  --Insert input ports below
    clock      : IN  std_logic;                    -- input bit example
    val        : IN  std_logic_vector(3 DOWNTO 0); -- input vector example
  ------------------------------------------------------------------------------
  --Insert output ports below
    max        : OUT std_logic;                    -- output bit example
    cpt        : OUT std_logic_vector(3 DOWNTO 0)  -- output vector example
    );
END latch_d_nor;

--------------------------------------------------------------------------------
--Complete your VHDL description below--FALTA
--------------------------------------------------------------------------------

ARCHITECTURE TypeArchitecture OF latch_d_nor IS

BEGIN


END TypeArchitecture;

// VHDL entity d_jk, as the project stores it:
--------------------------------------------------------------------------------
-- VERSAO DESCRITIVA
--------------------------------------------------------------------------------

LIBRARY ieee;
USE ieee.std_logic_1164.all;

ENTITY d_jk IS
  PORT (
  ------------------------------------------------------------------------------
  --Insert input ports below
    J, K, CLRN, PRN, CLK      : IN  std_logic;                  -- input bit example
  ------------------------------------------------------------------------------
  --Insert output ports below
    Q, QN         : OUT std_logic                   -- output bit example
    );
END d_jk;

--------------------------------------------------------------------------------
--Complete your VHDL description below
--------------------------------------------------------------------------------

ARCHITECTURE ff_jk_arch OF d_jk IS

signal qstate: std_logic;

BEGIN
    process(clk,prn,clrn)
    BEGIN
        if clrn = '0' then qstate <= '0';
        elsif prn = '0' then qstate <= '1';
        elsif clk = '1' and clk'event then
            if j = '1' and k = '1' then qstate <= not qstate;
            elsif j = '1' and k = '0' then qstate <= '1';
            elsif j = '0' and k = '1' then qstate <= '0';
        end if;
    end if;
end process;

Q <= qstate;
QN <= NOT qstate;

END ff_jk_arch;

// VHDL entity d_jk2, as the project stores it:
--------------------------------------------------------------------------------
-- VERSAO LOGICA
--------------------------------------------------------------------------------

LIBRARY ieee;
USE ieee.std_logic_1164.all;

ENTITY d_jk2 IS
  PORT (
  ------------------------------------------------------------------------------
  --Insert input ports below
    J, K, CLRN, PRN, CLK      : IN  std_logic;                  -- input bit example
  ------------------------------------------------------------------------------
  --Insert output ports below
    Q, QN         : OUT std_logic                   -- output bit example
    );
END d_jk2;

--------------------------------------------------------------------------------
--Complete your VHDL description below
--------------------------------------------------------------------------------

ARCHITECTURE ff_jk_arch OF d_jk2 IS

signal qstate: std_logic;

BEGIN
    process(clk,prn,clrn)
    BEGIN
        if clrn = '0' then qstate <= '0';
        elsif prn = '0' then qstate <= '1';
        elsif clk = '1' and clk'event then
            qstate <= (j and not qstate) or (not k and qstate);
        end if;

end process;

Q <= qstate;
QN <= NOT qstate;

END ff_jk_arch;

// VHDL entity d_j, as the project stores it:
--------------------------------------------------------------------------------
-- VERSAO DESCRITIVA
--------------------------------------------------------------------------------

LIBRARY ieee;
USE ieee.std_logic_1164.all;

entity d_j is
    port(
        T, CLRN, PRN, CLK : in  std_logic;      -- CLK, T e clear e preset

        Q, QN            : out std_logic      -- Saídas Q e Q invertido
    );
end d_j;

--------------------------------------------------------------------------------
--Complete your VHDL description below
-------------------------------------------------------------------------------

architecture ff_t_arch of d_j is

    signal qstate: std_logic;
begin
    process(clk, prn, clrn)
    begin
        if clrn = '0' then qstate <= '0';
        elsif prn = '0' then qstate <= '1';
        elsif clk = '1' and clk'event then
            if T = '1' then qstate <= not qstate;
            end if;
        end if;
    end process;

    q <= qstate;
    qn <= not qstate;

end ff_t_arch;

// VHDL entity d_j2, as the project stores it:
--------------------------------------------------------------------------------
-- VERSAO LOGICA
--------------------------------------------------------------------------------

LIBRARY ieee;
USE ieee.std_logic_1164.all;

entity d_j2 is
    port(
        T, CLRN, PRN, CLK : in  std_logic;      -- CLK, T e clear e preset

        Q, QN            : out std_logic      -- Saídas Q e Q invertido
    );
end d_j2;

architecture ff_t_arch of d_j2 is

    signal qstate: std_logic;
begin
    process(clk, prn, clrn)
    begin
        if clrn = '0' then qstate <= '0';
        elsif prn = '0' then qstate <= '1';
        elsif clk = '1' and clk'event then qstate <= T xor qstate;
        end if;
    end process;

    q <= qstate;
    qn <= not qstate;

end ff_t_arch;
