// Logisim project ex1.circ as structural Verilog
module ex1 (
  input  Z,
  input  UD,
  input  SST
);

  wire CLK_out;
  wire [6:0] cronometro_sincrono_1_qd_7s, cronometro_sincrono_1_qu_7s;

  Clock CLK (.out(CLK_out));
  cronometro_sincrono cronometro_sincrono_1 (
    .clk(CLK_out), .z(Z), .ud(UD), .sst(SST), .qu_7s(cronometro_sincrono_1_qu_7s),
    .qd_7s(cronometro_sincrono_1_qd_7s));
  _7_Segment_Display u_7_segment_display_1 (
    .g(cronometro_sincrono_1_qd_7s[0]), .f(cronometro_sincrono_1_qd_7s[1]),
    .a(cronometro_sincrono_1_qd_7s[6]), .b(cronometro_sincrono_1_qd_7s[5]),
    .e(cronometro_sincrono_1_qd_7s[2]), .d(cronometro_sincrono_1_qd_7s[3]), .c(cronometro_sincrono_1_qd_7s[4]));  // open: dp
  _7_Segment_Display u_7_segment_display_2 (
    .g(cronometro_sincrono_1_qu_7s[0]), .f(cronometro_sincrono_1_qu_7s[1]),
    .a(cronometro_sincrono_1_qu_7s[6]), .b(cronometro_sincrono_1_qu_7s[5]),
    .e(cronometro_sincrono_1_qu_7s[2]), .d(cronometro_sincrono_1_qu_7s[3]), .c(cronometro_sincrono_1_qu_7s[4]));  // open: dp
endmodule

module ex2 (
);

  wire CLK_out, start_out;
  wire [6:0] sequencia_ra_vhdl_1_lsd, sequencia_ra_vhdl_1_msd;

  Clock CLK (.out(CLK_out));
  Button start (.out(start_out));
  sequencia_ra_vhdl sequencia_ra_vhdl_1 (
    .clk(CLK_out), .start(start_out), .msd(sequencia_ra_vhdl_1_msd), .lsd(sequencia_ra_vhdl_1_lsd));
  _7_Segment_Display u_7_segment_display_1 (
    .g(sequencia_ra_vhdl_1_msd[0]), .f(sequencia_ra_vhdl_1_msd[1]), .a(sequencia_ra_vhdl_1_msd[6]),
    .b(sequencia_ra_vhdl_1_msd[5]), .e(sequencia_ra_vhdl_1_msd[2]), .d(sequencia_ra_vhdl_1_msd[3]),
    .c(sequencia_ra_vhdl_1_msd[4]));  // open: dp
  _7_Segment_Display u_7_segment_display_2 (
    .g(sequencia_ra_vhdl_1_lsd[0]), .f(sequencia_ra_vhdl_1_lsd[1]), .a(sequencia_ra_vhdl_1_lsd[6]),
    .b(sequencia_ra_vhdl_1_lsd[5]), .e(sequencia_ra_vhdl_1_lsd[2]), .d(sequencia_ra_vhdl_1_lsd[3]),
    .c(sequencia_ra_vhdl_1_lsd[4]));  // open: dp
endmodule

// VHDL entity cronometro_sincrono, as the project stores it:
library ieee;
use ieee.std_logic_1164.all;
use ieee.std_logic_unsigned.all;

entity cronometro_sincrono is
    port (
        clk, z, ud, sst : in  std_logic; 
        qu_7s, qd_7s    : out std_logic_vector(6 downto 0)
    );
end cronometro_sincrono;

architecture cronometro_sincrono_arch of cronometro_sincrono is
    signal u : std_logic_vector(3 downto 0);
    signal d : std_logic_vector(2 downto 0);
begin

    proc: process(clk, z)
    begin
        if z = '1' then
            -- Reset assíncrono
            if ud = '1' then
                u <= "0000";
                d <= "000";
            else
                u <= "1001";
                d <= "101";
            end if;
            
        elsif rising_edge(clk) then
            -- Contagem só ocorre se sst = '1'
            if sst = '1' then
                if ud = '1' then
                    -- Contagem progressiva (UP): 00 até 59
                    if u < "1001" then
                        u <= u + "0001";
                    else
                        u <= "0000";
                        if d < "101" then
                            d <= d + "001";
                        else 
                            d <= "000";
                        end if;
                    end if;
                else
                    -- Contagem regressiva (DOWN): 59 até 00
                    if u > "0000" then
                        u <= u - "0001";
                    else
                        u <= "1001";
                        if d > "000" then
                            d <= d - "001";
                        else 
                            d <= "101";
                        end if;
                    end if;
                end if;
            end if;
        end if;
    end process proc;

    -- Decodificadores 7 segmentos (unidades)
    with u select
        qu_7s <= "1111110" when "0000",
                 "0110000" when "0001",
                 "1101101" when "0010",
                 "1111001" when "0011",
                 "0110011" when "0100",
                 "1011011" when "0101",
                 "1011111" when "0110",
                 "1110000" when "0111",
                 "1111111" when "1000",
                 "1110011" when "1001",
                 "0000000" when others;

    -- Decodificador 7 segmentos (dezenas)
    with d select
        qd_7s <= "1111110" when "000",
                 "0110000" when "001",
                 "1101101" when "010",
                 "1111001" when "011",
                 "0110011" when "100",
                 "1011011" when "101",
                 "0000000" when others;

end cronometro_sincrono_arch;

// VHDL entity sequencia_ra_vhdl, as the project stores it:
library ieee;
use ieee.std_logic_1164.all;
use ieee.std_logic_unsigned.all;

entity sequencia_ra_vhdl is
    port (
        clk, start : in  std_logic;
        msd, lsd   : out std_logic_vector(6 downto 0)                
    );
end sequencia_ra_vhdl;

architecture sequencia_qualquer_arch of sequencia_ra_vhdl is
    signal contador: std_logic_vector(4 downto 0) := "00000";
    signal rodando: std_logic := '0';
    signal start_last: std_logic := '0';
begin
    processo: process(clk, start)
    begin
        if rising_edge(clk) then
            -- Detecção de borda de subida do botão start
            if start = '1' and start_last = '0' and rodando = '0' then
                rodando <= '1';
                contador <= "00000";
            end if;
            start_last <= start;
            
            -- Sequência em execução
            if rodando = '1' then
                if contador < "10000" then  -- 16 passos (0 a 15)
                    contador <= contador + "00001";
                else
                    rodando <= '0';  -- Volta ao repouso
                    contador <= "00000";
                end if;
            end if;
        end if;
    end process processo;

    -- Lógica combinacional para displays
    sequencia: process(contador, rodando)
    begin
        if rodando = '0' then
            -- Estado de repouso
            msd <= "0000000";  -- Apagado
            lsd <= "0000001";  -- Hífen (-)
        else
            -- Sequência: 2U 6 2T 4 1U 7 6T - 6U 7 1T 4 2U 6 2T -
            case contador is
                when "00000" => msd <= "1100111"; lsd <= "1101101"; -- U, 2
                when "00001" => msd <= "0000000"; lsd <= "1011111"; -- -, 6
                when "00010" => msd <= "1110001"; lsd <= "1101101"; -- T, 2
                when "00011" => msd <= "0000000"; lsd <= "0110011"; -- -, 4
                when "00100" => msd <= "1100111"; lsd <= "0110000"; -- U, 1
                when "00101" => msd <= "0000000"; lsd <= "1110000"; -- -, 7
                when "00110" => msd <= "1110001"; lsd <= "1011111"; -- T, 6
                when "00111" => msd <= "0000000"; lsd <= "0000001"; -- -, -
                when "01000" => msd <= "1100111"; lsd <= "1011111"; -- U, 6
                when "01001" => msd <= "0000000"; lsd <= "1110000"; -- -, 7
                when "01010" => msd <= "1110001"; lsd <= "0110000"; -- T, 1
                when "01011" => msd <= "0000000"; lsd <= "0110011"; -- -, 4
                when "01100" => msd <= "1100111"; lsd <= "1101101"; -- U, 2
                when "01101" => msd <= "0000000"; lsd <= "1011111"; -- -, 6
                when "01110" => msd <= "1110001"; lsd <= "1101101"; -- T, 2
                when "01111" => msd <= "0000000"; lsd <= "0000001"; -- -, -
                when others  => msd <= "0000000"; lsd <= "0000001"; -- Repouso
            end case;
        end if;
    end process sequencia;

end sequencia_qualquer_arch;
