// Logisim project Aula_03_ex_01.circ as structural Verilog: 2 circuits, main circuit main
module main (
  input  [3:0] in_1
);

  wire undriven, undriven_2, undriven_3, undriven_4, undriven_5;
  wire [1:0] undriven_6;

  dec_7s_muxes dec_7s_muxes_1 ();  // open: KLMN, out_2
  _7_Segment_Display u_7_segment_display_1 (
    .g(undriven_6[0]), .f(undriven_6[1]), .a(undriven), .b(undriven_2), .e(undriven_5), .d(undriven_4),
    .c(undriven_3));  // open: dp
endmodule

module dec_7s_muxes (
  input  [3:0] KLMN,
  output [6:0] out_2
);

  Multiplexer #(.select(4)) multiplexer_1 (
    .in0(1'b1), .in1(1'b0), .in2(1'b1), .in3(1'b1), .in4(1'b0), .in5(1'b1), .in6(1'b1), .in7(1'b1),
    .in8(1'b1), .in9(1'b1), .in10(1'b1), .in11(1'b0), .in12(1'b1), .in13(1'b0), .in14(1'b1), .in15(1'b1),
    .sel(KLMN));  // open: out

  // Other names for the same wires on the sheet: N = KLMN[0]; M = KLMN[1]; L = KLMN[2]; K = KLMN[3]; G = out_2[0];
  //   F = out_2[1]; E = out_2[2]; D = out_2[3]; C = out_2[4]; B = out_2[5]; A = out_2[6]
endmodule
